# Fritzing sketch Color Detector (saved by Fritzing 0.9.3b)
breadboards: 1

parts:
  Part2 = Arduino Nano (Rev3.0)
  IIC3 = IIC Convterter [part_number="LCD 20 x 4" package=converter]
  U1 = LCD-16X2 [package=lcd-16x2]  # not connected
  TSC3200 = TCS230 Color Sensor

nets:
  GND: Part2.GND, IIC3.GND, TSC3200.Gnd, TSC3200.OE
  N1: Part2.D4, TSC3200.S0
  N2: Part2.D5, TSC3200.S1
  N3: Part2.D6, TSC3200.S2
  N4: Part2.D7, TSC3200.S3
  N5: Part2.D8, TSC3200.Out
  VCC: Part2.VIN, IIC3.Vcc, TSC3200.Vcc
  N6: Part2.A5, IIC3.SCL
  N7: Part2.A4, IIC3.SDA

custom parts:
  IIC Convterter: Parallel to IIC Converter for HD44780 family LCDs
  TCS230 Color Sensor: TCS230
